# Fritzing sketch schema (saved by Fritzing 0.9.2b)
breadboards: 1

parts:
  Composant1 = Arduino Uno (Rev3) - ICSP
  J1 = screw terminal, 6 pins  # not connected
  J2 = Screw terminal - 2 pins [package=THT]
  J3 = Screw terminal - 2 pins [package=THT]
  R1 = Resistor [tolerance=±5% resistance=220 package=THT]
  R2 = Resistor [tolerance=±5% resistance=220 package=THT]
  J4 = Screw terminal - 2 pins [package=THT]
  J5 = Screw terminal - 2 pins [package=THT]

nets:
  N1: Composant1.A4/SDA, J2.pin1, R1.Pin_1
  N2: Composant1.A5/SCL, J3.pin1, R2.Pin_1
  N3: Composant1.D12/MISO, J4.pin1
  N4: Composant1.D13/SCK, J5.pin1
  N5: Composant1.GND, J2.pin2, J3.pin2, J4.pin2, J5.pin2
  N6: Composant1.5V, R1.Pin_0, R2.Pin_0
